# Fritzing sketch iot-raspi-multithreading (saved by Fritzing 0.9.9b)
breadboards: 2

parts:
  LED1 = LED - 5mm [color="Green (565nm)" current=0.030 package="5 mm [THT]"]
  LED2 = LED - 5mm [color="Yellow (595nm)" current=0.030 package="5 mm [THT]"]
  R4 = Resistor [tolerance=±5% power=0.25 resistance=560 package=THT]
  R5 = Resistor [tolerance=±5% power=0.25 resistance=560 package=THT]
  LED3 = LED - 5mm [color="Red (633nm)" current=0.030 package="5 mm [THT]"]
  R6 = Resistor [tolerance=±5% power=0.25 resistance=560 package=THT]
  R7 = Trimmer Potentiometer [maximum_resistance=10kΩ package=THT]
  R8 = Trimmer Potentiometer [maximum_resistance=10kΩ package=THT]
  S1 = Pushbutton [package="[THT]"]
  S2 = Pushbutton [package="[THT]"]
  S3 = Pushbutton [package="[THT]"]
  LCD1 = LCD screen
  R9 = Resistor [tolerance=±5% power=0.25 resistance=220 package=THT]
  R10 = Trimmer Potentiometer [maximum_resistance=10kΩ package=THT]
  Mod1 = Raspberry Pi 4B
  ADC1 = MCP3008 [package=dil16]
  C5 = Ceramic Capacitor [capacitance=100nF voltage=35V package="100 mil [THT, multilayer]"]
  C6 = Ceramic Capacitor [capacitance=100nF voltage=35V package="100 mil [THT, multilayer]"]
  C7 = Electrolytic Capacitor [capacitance=1µF voltage=35V package="100 mil [THT, electrolytic]"]

nets:
  N1: LED1.cathode, R6.Pin_0
  N2: LED1.anode, Mod1.GPIO22
  N3: LED2.cathode, R5.Pin_0
  N4: LED2.anode, Mod1.GPIO27
  N5: R4.Pin_0, LED3.cathode
  VSS: R4.Pin_1, R5.Pin_1, R6.Pin_1, S1.Pin_3, S1.Pin_4, S2.Pin_3, S2.Pin_4, S3.Pin_3, S3.Pin_4, LCD1.VSS, LCD1.R/W, LCD1.LED-, R10.leg2, Mod1.GND, ADC1.DGND, ADC1.AGND, C6.1, C7.-
  N6: LED3.anode, Mod1.GPIO17
  N7: R7.leg1, R8.leg1, C5.1
  N8: R7.wiper, ADC1.CH1
  N9: R7.leg2, R8.leg2, C5.0
  N10: R8.wiper, ADC1.CH0
  N11: S1.Pin_1, S1.Pin_2, Mod1.GPIO18
  N12: S2.Pin_1, S2.Pin_2, Mod1.GPIO23
  N13: S3.Pin_1, S3.Pin_2, Mod1.GPIO24
  VDD: LCD1.VDD, R9.Pin_0, R10.leg1, Mod1.3V3
  N14: LCD1.V0, R10.wiper
  N15: LCD1.LED+, R9.Pin_1
  5V: Mod1.5V, ADC1.VDD, C6.0, C7.+
  N16: Mod1.GPIO10, ADC1.Din
  N17: Mod1.GPIO9, ADC1.Dout
  N18: Mod1.GPIO11, ADC1.CLK
  N19: Mod1.GPIO8, ADC1.CS/SHDN

notes:
  iot-raspi-multithreading
  red
  yellow
  green
  fast   slow   stop
